# Fritzing sketch SPI (saved by Fritzing 0.9.2b)
breadboards: 1

parts:
  J2 = Infrared Proximity Sensor
  Raspberry_Pi1 = Raspberry Pi 2
  J3 = Infrared Proximity Sensor
  IC1 = IC, DIP package, 16 pins [chip_label=IC]

nets:
  N1: J2.Vout, IC1.pin1
  GND: J2.GND, Raspberry_Pi1.GND, J3.GND, IC1.pin9, IC1.pin14
  VCC: J2.Vcc, Raspberry_Pi1.5V, J3.Vcc, IC1.pin15, IC1.pin16
  N2: Raspberry_Pi1.GPIO10, IC1.pin11
  N3: Raspberry_Pi1.GPIO9, IC1.pin12
  N4: Raspberry_Pi1.GPIO11, IC1.pin13
  N5: Raspberry_Pi1.GPIO8, IC1.pin10
  N6: J3.Vout, IC1.pin2
